// Logisim project logisim files.circ as structural Verilog: 11 circuits, main circuit restoring_block
// Q7
module restoring (
  input  B7,
  input  B6,
  input  B5,
  input  B4,
  input  B3,
  input  B2,
  input  B1,
  input  B0,
  input  A7,
  input  A6,
  input  A5,
  input  A4,
  input  A3,
  input  A2,
  input  A1,
  input  A0,
  output Q7,
  output Q6,
  output Q5,
  output Q4,
  output Q3,
  output Q2,
  output Q1,
  output Q0,
  output R7,
  output R6,
  output R5,
  output R4,
  output R3,
  output R2,
  output R1,
  output R0
);

  wire not_1_out, not_2_out, not_3_out, not_4_out, not_5_out, not_6_out, not_7_out, not_8_out,
       restoring_block_2_cout, restoring_block_2_z, restoring_block_3_cout, restoring_block_3_z,
       restoring_block_6_cout, restoring_block_6_z, restoring_block_8_cout, restoring_block_8_z,
       restoring_block_10_cout, restoring_block_10_z, restoring_block_11_cout, restoring_block_11_z,
       restoring_block_14_cout, restoring_block_14_z, restoring_block_15_cout, restoring_block_17_cout,
       restoring_block_17_z, restoring_block_18_cout, restoring_block_18_z, restoring_block_19_cout,
       restoring_block_19_z, restoring_block_20_cout, restoring_block_20_z, restoring_block_21_cout,
       restoring_block_21_z, restoring_block_22_cout, restoring_block_22_z, restoring_block_23_cout,
       restoring_block_23_z, restoring_block_24_cout, restoring_block_25_cout, restoring_block_25_z,
       restoring_block_26_cout, restoring_block_26_z, restoring_block_27_cout, restoring_block_27_z,
       restoring_block_28_cout, restoring_block_28_z, restoring_block_29_cout, restoring_block_29_z,
       restoring_block_30_cout, restoring_block_30_z, restoring_block_31_cout, restoring_block_31_z,
       restoring_block_32_cout, restoring_block_33_cout, restoring_block_33_z, restoring_block_34_cout,
       restoring_block_34_z, restoring_block_35_cout, restoring_block_35_z, restoring_block_36_cout,
       restoring_block_36_z, restoring_block_37_cout, restoring_block_37_z, restoring_block_38_cout,
       restoring_block_38_z, restoring_block_39_cout, restoring_block_39_z, restoring_block_40_cout,
       restoring_block_40_z, restoring_block_41_cout, restoring_block_41_z, restoring_block_42_cout,
       restoring_block_42_z, restoring_block_43_cout, restoring_block_43_z, restoring_block_44_cout,
       restoring_block_44_z, restoring_block_45_cout, restoring_block_45_z, restoring_block_46_cout,
       restoring_block_46_z, restoring_block_47_cout, restoring_block_48_cout, restoring_block_49_cout,
       restoring_block_49_z, restoring_block_50_cout, restoring_block_50_z, restoring_block_51_cout,
       restoring_block_51_z, restoring_block_52_cout, restoring_block_52_z, restoring_block_53_cout,
       restoring_block_53_z, restoring_block_54_cout, restoring_block_54_z, restoring_block_55_cout,
       restoring_block_55_z, restoring_block_56_cout, restoring_block_57_cout, restoring_block_57_z,
       restoring_block_58_cout, restoring_block_58_z, restoring_block_59_cout, restoring_block_59_z,
       restoring_block_60_cout, restoring_block_60_z, restoring_block_61_cout, restoring_block_61_z,
       restoring_block_62_cout, restoring_block_62_z, restoring_block_63_cout, restoring_block_63_z,
       restoring_block_64_cout;

  not not_1 (not_1_out, B7);
  not not_2 (not_2_out, B6);
  restoring_block restoring_block_1 (
    .A(1'b0), .B(not_1_out), .Cin(restoring_block_2_cout), .Cout(Q7), .Sel(Q7));  // open: Z
  restoring_block restoring_block_2 (
    .A(1'b0), .B(not_2_out), .Z(restoring_block_2_z), .Cin(restoring_block_17_cout),
    .Cout(restoring_block_2_cout), .Sel(Q7));
  restoring_block restoring_block_3 (
    .A(restoring_block_17_z), .B(not_2_out), .Z(restoring_block_3_z), .Cin(restoring_block_18_cout),
    .Cout(restoring_block_3_cout), .Sel(Q6));
  restoring_block restoring_block_4 (
    .A(restoring_block_2_z), .B(not_1_out), .Cin(restoring_block_3_cout), .Cout(Q6), .Sel(Q6));  // open: Z
  restoring_block restoring_block_5 (
    .A(restoring_block_3_z), .B(not_1_out), .Cin(restoring_block_6_cout), .Cout(Q5), .Sel(Q5));  // open: Z
  restoring_block restoring_block_6 (
    .A(restoring_block_18_z), .B(not_2_out), .Z(restoring_block_6_z), .Cin(restoring_block_19_cout),
    .Cout(restoring_block_6_cout), .Sel(Q5));
  restoring_block restoring_block_7 (
    .A(restoring_block_6_z), .B(not_1_out), .Cin(restoring_block_8_cout), .Cout(Q4), .Sel(Q4));  // open: Z
  restoring_block restoring_block_8 (
    .A(restoring_block_19_z), .B(not_2_out), .Z(restoring_block_8_z), .Cin(restoring_block_20_cout),
    .Cout(restoring_block_8_cout), .Sel(Q4));
  restoring_block restoring_block_9 (
    .A(restoring_block_8_z), .B(not_1_out), .Cin(restoring_block_10_cout), .Cout(Q3), .Sel(Q3));  // open: Z
  restoring_block restoring_block_10 (
    .A(restoring_block_20_z), .B(not_2_out), .Z(restoring_block_10_z), .Cin(restoring_block_21_cout),
    .Cout(restoring_block_10_cout), .Sel(Q3));
  restoring_block restoring_block_11 (
    .A(restoring_block_21_z), .B(not_2_out), .Z(restoring_block_11_z), .Cin(restoring_block_22_cout),
    .Cout(restoring_block_11_cout), .Sel(Q2));
  restoring_block restoring_block_12 (
    .A(restoring_block_10_z), .B(not_1_out), .Cin(restoring_block_11_cout), .Cout(Q2), .Sel(Q2));  // open: Z
  restoring_block restoring_block_13 (
    .A(restoring_block_11_z), .B(not_1_out), .Cin(restoring_block_14_cout), .Cout(Q1), .Sel(Q1));  // open: Z
  restoring_block restoring_block_14 (
    .A(restoring_block_22_z), .B(not_2_out), .Z(restoring_block_14_z), .Cin(restoring_block_23_cout),
    .Cout(restoring_block_14_cout), .Sel(Q1));
  restoring_block restoring_block_15 (
    .A(restoring_block_23_z), .B(not_2_out), .Z(R6), .Cin(restoring_block_24_cout),
    .Cout(restoring_block_15_cout), .Sel(Q0));
  restoring_block restoring_block_16 (
    .A(restoring_block_14_z), .B(not_1_out), .Z(R7), .Cin(restoring_block_15_cout), .Cout(Q0), .Sel(Q0));
  not not_3 (not_3_out, B5);
  restoring_block restoring_block_17 (
    .A(1'b0), .B(not_3_out), .Z(restoring_block_17_z), .Cin(restoring_block_25_cout),
    .Cout(restoring_block_17_cout), .Sel(Q7));
  restoring_block restoring_block_18 (
    .A(restoring_block_25_z), .B(not_3_out), .Z(restoring_block_18_z), .Cin(restoring_block_26_cout),
    .Cout(restoring_block_18_cout), .Sel(Q6));
  restoring_block restoring_block_19 (
    .A(restoring_block_26_z), .B(not_3_out), .Z(restoring_block_19_z), .Cin(restoring_block_27_cout),
    .Cout(restoring_block_19_cout), .Sel(Q5));
  restoring_block restoring_block_20 (
    .A(restoring_block_27_z), .B(not_3_out), .Z(restoring_block_20_z), .Cin(restoring_block_28_cout),
    .Cout(restoring_block_20_cout), .Sel(Q4));
  restoring_block restoring_block_21 (
    .A(restoring_block_28_z), .B(not_3_out), .Z(restoring_block_21_z), .Cin(restoring_block_29_cout),
    .Cout(restoring_block_21_cout), .Sel(Q3));
  restoring_block restoring_block_22 (
    .A(restoring_block_29_z), .B(not_3_out), .Z(restoring_block_22_z), .Cin(restoring_block_30_cout),
    .Cout(restoring_block_22_cout), .Sel(Q2));
  restoring_block restoring_block_23 (
    .A(restoring_block_30_z), .B(not_3_out), .Z(restoring_block_23_z), .Cin(restoring_block_31_cout),
    .Cout(restoring_block_23_cout), .Sel(Q1));
  restoring_block restoring_block_24 (
    .A(restoring_block_31_z), .B(not_3_out), .Z(R5), .Cin(restoring_block_32_cout),
    .Cout(restoring_block_24_cout), .Sel(Q0));
  not not_4 (not_4_out, B4);
  restoring_block restoring_block_25 (
    .A(1'b0), .B(not_4_out), .Z(restoring_block_25_z), .Cin(restoring_block_33_cout),
    .Cout(restoring_block_25_cout), .Sel(Q7));
  restoring_block restoring_block_26 (
    .A(restoring_block_33_z), .B(not_4_out), .Z(restoring_block_26_z), .Cin(restoring_block_36_cout),
    .Cout(restoring_block_26_cout), .Sel(Q6));
  restoring_block restoring_block_27 (
    .A(restoring_block_36_z), .B(not_4_out), .Z(restoring_block_27_z), .Cin(restoring_block_37_cout),
    .Cout(restoring_block_27_cout), .Sel(Q5));
  restoring_block restoring_block_28 (
    .A(restoring_block_37_z), .B(not_4_out), .Z(restoring_block_28_z), .Cin(restoring_block_39_cout),
    .Cout(restoring_block_28_cout), .Sel(Q4));
  restoring_block restoring_block_29 (
    .A(restoring_block_39_z), .B(not_4_out), .Z(restoring_block_29_z), .Cin(restoring_block_42_cout),
    .Cout(restoring_block_29_cout), .Sel(Q3));
  restoring_block restoring_block_30 (
    .A(restoring_block_42_z), .B(not_4_out), .Z(restoring_block_30_z), .Cin(restoring_block_43_cout),
    .Cout(restoring_block_30_cout), .Sel(Q2));
  restoring_block restoring_block_31 (
    .A(restoring_block_43_z), .B(not_4_out), .Z(restoring_block_31_z), .Cin(restoring_block_45_cout),
    .Cout(restoring_block_31_cout), .Sel(Q1));
  restoring_block restoring_block_32 (
    .A(restoring_block_45_z), .B(not_4_out), .Z(R4), .Cin(restoring_block_48_cout),
    .Cout(restoring_block_32_cout), .Sel(Q0));
  not not_5 (not_5_out, B3);
  not not_6 (not_6_out, B2);
  restoring_block restoring_block_33 (
    .A(1'b0), .B(not_5_out), .Z(restoring_block_33_z), .Cin(restoring_block_34_cout),
    .Cout(restoring_block_33_cout), .Sel(Q7));
  restoring_block restoring_block_34 (
    .A(1'b0), .B(not_6_out), .Z(restoring_block_34_z), .Cin(restoring_block_49_cout),
    .Cout(restoring_block_34_cout), .Sel(Q7));
  restoring_block restoring_block_35 (
    .A(restoring_block_49_z), .B(not_6_out), .Z(restoring_block_35_z), .Cin(restoring_block_50_cout),
    .Cout(restoring_block_35_cout), .Sel(Q6));
  restoring_block restoring_block_36 (
    .A(restoring_block_34_z), .B(not_5_out), .Z(restoring_block_36_z), .Cin(restoring_block_35_cout),
    .Cout(restoring_block_36_cout), .Sel(Q6));
  restoring_block restoring_block_37 (
    .A(restoring_block_35_z), .B(not_5_out), .Z(restoring_block_37_z), .Cin(restoring_block_38_cout),
    .Cout(restoring_block_37_cout), .Sel(Q5));
  restoring_block restoring_block_38 (
    .A(restoring_block_50_z), .B(not_6_out), .Z(restoring_block_38_z), .Cin(restoring_block_51_cout),
    .Cout(restoring_block_38_cout), .Sel(Q5));
  restoring_block restoring_block_39 (
    .A(restoring_block_38_z), .B(not_5_out), .Z(restoring_block_39_z), .Cin(restoring_block_40_cout),
    .Cout(restoring_block_39_cout), .Sel(Q4));
  restoring_block restoring_block_40 (
    .A(restoring_block_51_z), .B(not_6_out), .Z(restoring_block_40_z), .Cin(restoring_block_52_cout),
    .Cout(restoring_block_40_cout), .Sel(Q4));
  restoring_block restoring_block_41 (
    .A(restoring_block_52_z), .B(not_6_out), .Z(restoring_block_41_z), .Cin(restoring_block_53_cout),
    .Cout(restoring_block_41_cout), .Sel(Q3));
  restoring_block restoring_block_42 (
    .A(restoring_block_40_z), .B(not_5_out), .Z(restoring_block_42_z), .Cin(restoring_block_41_cout),
    .Cout(restoring_block_42_cout), .Sel(Q3));
  restoring_block restoring_block_43 (
    .A(restoring_block_41_z), .B(not_5_out), .Z(restoring_block_43_z), .Cin(restoring_block_44_cout),
    .Cout(restoring_block_43_cout), .Sel(Q2));
  restoring_block restoring_block_44 (
    .A(restoring_block_53_z), .B(not_6_out), .Z(restoring_block_44_z), .Cin(restoring_block_54_cout),
    .Cout(restoring_block_44_cout), .Sel(Q2));
  restoring_block restoring_block_45 (
    .A(restoring_block_44_z), .B(not_5_out), .Z(restoring_block_45_z), .Cin(restoring_block_46_cout),
    .Cout(restoring_block_45_cout), .Sel(Q1));
  restoring_block restoring_block_46 (
    .A(restoring_block_54_z), .B(not_6_out), .Z(restoring_block_46_z), .Cin(restoring_block_55_cout),
    .Cout(restoring_block_46_cout), .Sel(Q1));
  restoring_block restoring_block_47 (
    .A(restoring_block_55_z), .B(not_6_out), .Z(R2), .Cin(restoring_block_56_cout),
    .Cout(restoring_block_47_cout), .Sel(Q0));
  restoring_block restoring_block_48 (
    .A(restoring_block_46_z), .B(not_5_out), .Z(R3), .Cin(restoring_block_47_cout),
    .Cout(restoring_block_48_cout), .Sel(Q0));
  not not_7 (not_7_out, B1);
  restoring_block restoring_block_49 (
    .A(1'b0), .B(not_7_out), .Z(restoring_block_49_z), .Cin(restoring_block_57_cout),
    .Cout(restoring_block_49_cout), .Sel(Q7));
  restoring_block restoring_block_50 (
    .A(restoring_block_57_z), .B(not_7_out), .Z(restoring_block_50_z), .Cin(restoring_block_58_cout),
    .Cout(restoring_block_50_cout), .Sel(Q6));
  restoring_block restoring_block_51 (
    .A(restoring_block_58_z), .B(not_7_out), .Z(restoring_block_51_z), .Cin(restoring_block_59_cout),
    .Cout(restoring_block_51_cout), .Sel(Q5));
  restoring_block restoring_block_52 (
    .A(restoring_block_59_z), .B(not_7_out), .Z(restoring_block_52_z), .Cin(restoring_block_60_cout),
    .Cout(restoring_block_52_cout), .Sel(Q4));
  restoring_block restoring_block_53 (
    .A(restoring_block_60_z), .B(not_7_out), .Z(restoring_block_53_z), .Cin(restoring_block_61_cout),
    .Cout(restoring_block_53_cout), .Sel(Q3));
  restoring_block restoring_block_54 (
    .A(restoring_block_61_z), .B(not_7_out), .Z(restoring_block_54_z), .Cin(restoring_block_62_cout),
    .Cout(restoring_block_54_cout), .Sel(Q2));
  restoring_block restoring_block_55 (
    .A(restoring_block_62_z), .B(not_7_out), .Z(restoring_block_55_z), .Cin(restoring_block_63_cout),
    .Cout(restoring_block_55_cout), .Sel(Q1));
  restoring_block restoring_block_56 (
    .A(restoring_block_63_z), .B(not_7_out), .Z(R1), .Cin(restoring_block_64_cout),
    .Cout(restoring_block_56_cout), .Sel(Q0));
  not not_8 (not_8_out, B0);
  restoring_block restoring_block_57 (
    .A(A7), .B(not_8_out), .Z(restoring_block_57_z), .Cin(1'b1), .Cout(restoring_block_57_cout), .Sel(Q7));
  restoring_block restoring_block_58 (
    .A(A6), .B(not_8_out), .Z(restoring_block_58_z), .Cin(1'b1), .Cout(restoring_block_58_cout), .Sel(Q6));
  restoring_block restoring_block_59 (
    .A(A5), .B(not_8_out), .Z(restoring_block_59_z), .Cin(1'b1), .Cout(restoring_block_59_cout), .Sel(Q5));
  restoring_block restoring_block_60 (
    .A(A4), .B(not_8_out), .Z(restoring_block_60_z), .Cin(1'b1), .Cout(restoring_block_60_cout), .Sel(Q4));
  restoring_block restoring_block_61 (
    .A(A3), .B(not_8_out), .Z(restoring_block_61_z), .Cin(1'b1), .Cout(restoring_block_61_cout), .Sel(Q3));
  restoring_block restoring_block_62 (
    .A(A2), .B(not_8_out), .Z(restoring_block_62_z), .Cin(1'b1), .Cout(restoring_block_62_cout), .Sel(Q2));
  restoring_block restoring_block_63 (
    .A(A1), .B(not_8_out), .Z(restoring_block_63_z), .Cin(1'b1), .Cout(restoring_block_63_cout), .Sel(Q1));
  restoring_block restoring_block_64 (
    .A(A0), .B(not_8_out), .Z(R0), .Cin(1'b1), .Cout(restoring_block_64_cout), .Sel(Q0));
endmodule

// re
module restoring_block (
  input  Cin,
  input  A,
  input  B,
  input  Sel,
  output Z,
  output Cout
);

  wire adder_1_out;

  Adder #(.width(1)) adder_1 (.a(A), .b(B), .out(adder_1_out), .cin(Cin), .cout(Cout));
  Multiplexer #(.enable("false")) multiplexer_1 (.in0(A), .in1(adder_1_out), .out(Z), .sel(Sel));
endmodule

module nonrestoring (
  input  B7,
  input  B6,
  input  B5,
  input  B4,
  input  B3,
  input  B2,
  input  B1,
  input  B0,
  input  A7,
  input  A6,
  input  A6_2,
  input  A6_3,
  input  A6_4,
  input  A6_5,
  input  A6_6,
  input  A6_7,
  output Q,
  output Q_2,
  output Q_3,
  output Q_4,
  output Q_5,
  output Q_6,
  output Q_7,
  output Q_8,
  output R7,
  output R6,
  output R5,
  output R4,
  output R3,
  output R2,
  output R1,
  output R0
);

  wire nonrestoring_block_1_cout, nonrestoring_block_1_z, nonrestoring_block_4_cout, nonrestoring_block_4_z,
       nonrestoring_block_6_cout, nonrestoring_block_6_z, nonrestoring_block_7_cout, nonrestoring_block_7_z,
       nonrestoring_block_10_cout, nonrestoring_block_10_z, nonrestoring_block_12_cout,
       nonrestoring_block_12_z, nonrestoring_block_14_cout, nonrestoring_block_14_z,
       nonrestoring_block_15_cout, nonrestoring_block_15_z, nonrestoring_block_16_z,
       nonrestoring_block_17_cout, nonrestoring_block_17_z, nonrestoring_block_18_cout,
       nonrestoring_block_18_z, nonrestoring_block_19_cout, nonrestoring_block_19_z,
       nonrestoring_block_20_cout, nonrestoring_block_20_z, nonrestoring_block_21_cout,
       nonrestoring_block_21_z, nonrestoring_block_22_cout, nonrestoring_block_22_z,
       nonrestoring_block_23_cout, nonrestoring_block_23_z, nonrestoring_block_24_cout,
       nonrestoring_block_24_z, nonrestoring_block_25_cout, nonrestoring_block_25_z,
       nonrestoring_block_26_cout, nonrestoring_block_26_z, nonrestoring_block_27_cout,
       nonrestoring_block_27_z, nonrestoring_block_28_cout, nonrestoring_block_28_z,
       nonrestoring_block_29_cout, nonrestoring_block_29_z, nonrestoring_block_30_cout,
       nonrestoring_block_30_z, nonrestoring_block_31_cout, nonrestoring_block_31_z,
       nonrestoring_block_32_cout, nonrestoring_block_32_z, nonrestoring_block_33_cout,
       nonrestoring_block_33_z, nonrestoring_block_34_cout, nonrestoring_block_34_z,
       nonrestoring_block_35_cout, nonrestoring_block_35_z, nonrestoring_block_36_cout,
       nonrestoring_block_36_z, nonrestoring_block_37_cout, nonrestoring_block_37_z,
       nonrestoring_block_38_cout, nonrestoring_block_38_z, nonrestoring_block_39_cout,
       nonrestoring_block_39_z, nonrestoring_block_40_cout, nonrestoring_block_40_z,
       nonrestoring_block_41_cout, nonrestoring_block_41_z, nonrestoring_block_42_cout,
       nonrestoring_block_42_z, nonrestoring_block_43_cout, nonrestoring_block_43_z,
       nonrestoring_block_44_cout, nonrestoring_block_44_z, nonrestoring_block_45_cout,
       nonrestoring_block_45_z, nonrestoring_block_46_cout, nonrestoring_block_46_z,
       nonrestoring_block_47_cout, nonrestoring_block_47_z, nonrestoring_block_48_cout,
       nonrestoring_block_48_z, nonrestoring_block_49_cout, nonrestoring_block_49_z,
       nonrestoring_block_50_cout, nonrestoring_block_50_z, nonrestoring_block_51_cout,
       nonrestoring_block_51_z, nonrestoring_block_52_cout, nonrestoring_block_52_z,
       nonrestoring_block_53_cout, nonrestoring_block_53_z, nonrestoring_block_54_cout,
       nonrestoring_block_54_z, nonrestoring_block_55_cout, nonrestoring_block_55_z,
       nonrestoring_block_56_cout, nonrestoring_block_56_z, nonrestoring_block_57_cout,
       nonrestoring_block_57_z, nonrestoring_block_58_cout, nonrestoring_block_58_z,
       nonrestoring_block_59_cout, nonrestoring_block_59_z, nonrestoring_block_60_cout,
       nonrestoring_block_60_z, nonrestoring_block_61_cout, nonrestoring_block_61_z,
       nonrestoring_block_62_cout, nonrestoring_block_62_z, nonrestoring_block_63_cout,
       nonrestoring_block_63_z, nonrestoring_block_64_cout, nonrestoring_block_64_z,
       nonrestoring_block_65_cout, nonrestoring_block_65_z, nonrestoring_block_66_cout,
       nonrestoring_block_66_z, nonrestoring_block_67_cout, nonrestoring_block_67_z,
       nonrestoring_block_68_cout, nonrestoring_block_68_z, nonrestoring_block_69_cout,
       nonrestoring_block_69_z, nonrestoring_block_70_cout, nonrestoring_block_70_z,
       nonrestoring_block_71_cout, nonrestoring_block_71_z, nonrestoring_block_72_cout,
       nonrestoring_block_72_z, restoring_block_2_cout, restoring_block_3_cout, restoring_block_4_cout,
       restoring_block_5_cout, restoring_block_6_cout, restoring_block_7_cout, restoring_block_8_cout;

  nonrestoring_block nonrestoring_block_1 (
    .A(1'b0), .Z(nonrestoring_block_1_z), .Cin(nonrestoring_block_17_cout), .Sel(1'b1),
    .Cout(nonrestoring_block_1_cout), .B(B7));
  nonrestoring_block nonrestoring_block_2 (
    .A(1'b0), .Cin(nonrestoring_block_1_cout), .Sel(1'b1), .Cout(Q), .B(1'b0));  // open: Z
  nonrestoring_block nonrestoring_block_3 (
    .A(nonrestoring_block_1_z), .Cin(nonrestoring_block_4_cout), .Sel(Q), .Cout(Q_2), .B(1'b0));  // open: Z
  nonrestoring_block nonrestoring_block_4 (
    .A(nonrestoring_block_17_z), .Z(nonrestoring_block_4_z), .Cin(nonrestoring_block_18_cout), .Sel(Q),
    .Cout(nonrestoring_block_4_cout), .B(B7));
  nonrestoring_block nonrestoring_block_5 (
    .A(nonrestoring_block_4_z), .Cin(nonrestoring_block_6_cout), .Sel(Q_2), .Cout(Q_3), .B(1'b0));  // open: Z
  nonrestoring_block nonrestoring_block_6 (
    .A(nonrestoring_block_18_z), .Z(nonrestoring_block_6_z), .Cin(nonrestoring_block_19_cout), .Sel(Q_2),
    .Cout(nonrestoring_block_6_cout), .B(B7));
  nonrestoring_block nonrestoring_block_7 (
    .A(nonrestoring_block_19_z), .Z(nonrestoring_block_7_z), .Cin(nonrestoring_block_20_cout), .Sel(Q_3),
    .Cout(nonrestoring_block_7_cout), .B(B7));
  nonrestoring_block nonrestoring_block_8 (
    .A(nonrestoring_block_6_z), .Cin(nonrestoring_block_7_cout), .Sel(Q_3), .Cout(Q_4), .B(1'b0));  // open: Z
  nonrestoring_block nonrestoring_block_9 (
    .A(nonrestoring_block_7_z), .Cin(nonrestoring_block_10_cout), .Sel(Q_4), .Cout(Q_5), .B(1'b0));  // open: Z
  nonrestoring_block nonrestoring_block_10 (
    .A(nonrestoring_block_20_z), .Z(nonrestoring_block_10_z), .Cin(nonrestoring_block_21_cout), .Sel(Q_4),
    .Cout(nonrestoring_block_10_cout), .B(B7));
  nonrestoring_block nonrestoring_block_11 (
    .A(nonrestoring_block_10_z), .Cin(nonrestoring_block_12_cout), .Sel(Q_5), .Cout(Q_6), .B(1'b0));  // open: Z
  nonrestoring_block nonrestoring_block_12 (
    .A(nonrestoring_block_21_z), .Z(nonrestoring_block_12_z), .Cin(nonrestoring_block_22_cout), .Sel(Q_5),
    .Cout(nonrestoring_block_12_cout), .B(B7));
  nonrestoring_block nonrestoring_block_13 (
    .A(nonrestoring_block_12_z), .Cin(nonrestoring_block_14_cout), .Sel(Q_6), .Cout(Q_7), .B(1'b0));  // open: Z
  nonrestoring_block nonrestoring_block_14 (
    .A(nonrestoring_block_22_z), .Z(nonrestoring_block_14_z), .Cin(nonrestoring_block_23_cout), .Sel(Q_6),
    .Cout(nonrestoring_block_14_cout), .B(B7));
  nonrestoring_block nonrestoring_block_15 (
    .A(nonrestoring_block_23_z), .Z(nonrestoring_block_15_z), .Cin(nonrestoring_block_24_cout), .Sel(Q_7),
    .Cout(nonrestoring_block_15_cout), .B(B7));
  nonrestoring_block nonrestoring_block_16 (
    .A(nonrestoring_block_14_z), .Z(nonrestoring_block_16_z), .Cin(nonrestoring_block_15_cout), .Sel(Q_7),
    .Cout(Q_8), .B(1'b0));
  restoring_block restoring_block_1 (
    .A(nonrestoring_block_15_z), .B(B7), .Z(R7), .Cin(restoring_block_2_cout), .Sel(nonrestoring_block_16_z));  // open: Cout
  nonrestoring_block nonrestoring_block_17 (
    .A(1'b0), .Z(nonrestoring_block_17_z), .Cin(nonrestoring_block_25_cout), .Sel(1'b1),
    .Cout(nonrestoring_block_17_cout), .B(B6));
  nonrestoring_block nonrestoring_block_18 (
    .A(nonrestoring_block_25_z), .Z(nonrestoring_block_18_z), .Cin(nonrestoring_block_26_cout), .Sel(Q),
    .Cout(nonrestoring_block_18_cout), .B(B6));
  nonrestoring_block nonrestoring_block_19 (
    .A(nonrestoring_block_26_z), .Z(nonrestoring_block_19_z), .Cin(nonrestoring_block_27_cout), .Sel(Q_2),
    .Cout(nonrestoring_block_19_cout), .B(B6));
  nonrestoring_block nonrestoring_block_20 (
    .A(nonrestoring_block_27_z), .Z(nonrestoring_block_20_z), .Cin(nonrestoring_block_28_cout), .Sel(Q_3),
    .Cout(nonrestoring_block_20_cout), .B(B6));
  nonrestoring_block nonrestoring_block_21 (
    .A(nonrestoring_block_28_z), .Z(nonrestoring_block_21_z), .Cin(nonrestoring_block_29_cout), .Sel(Q_4),
    .Cout(nonrestoring_block_21_cout), .B(B6));
  nonrestoring_block nonrestoring_block_22 (
    .A(nonrestoring_block_29_z), .Z(nonrestoring_block_22_z), .Cin(nonrestoring_block_30_cout), .Sel(Q_5),
    .Cout(nonrestoring_block_22_cout), .B(B6));
  nonrestoring_block nonrestoring_block_23 (
    .A(nonrestoring_block_30_z), .Z(nonrestoring_block_23_z), .Cin(nonrestoring_block_31_cout), .Sel(Q_6),
    .Cout(nonrestoring_block_23_cout), .B(B6));
  nonrestoring_block nonrestoring_block_24 (
    .A(nonrestoring_block_31_z), .Z(nonrestoring_block_24_z), .Cin(nonrestoring_block_32_cout), .Sel(Q_7),
    .Cout(nonrestoring_block_24_cout), .B(B6));
  restoring_block restoring_block_2 (
    .A(nonrestoring_block_24_z), .B(B6), .Z(R6), .Cin(restoring_block_3_cout), .Cout(restoring_block_2_cout),
    .Sel(nonrestoring_block_16_z));
  nonrestoring_block nonrestoring_block_25 (
    .A(1'b0), .Z(nonrestoring_block_25_z), .Cin(nonrestoring_block_33_cout), .Sel(1'b1),
    .Cout(nonrestoring_block_25_cout), .B(B5));
  nonrestoring_block nonrestoring_block_26 (
    .A(nonrestoring_block_33_z), .Z(nonrestoring_block_26_z), .Cin(nonrestoring_block_35_cout), .Sel(Q),
    .Cout(nonrestoring_block_26_cout), .B(B5));
  nonrestoring_block nonrestoring_block_27 (
    .A(nonrestoring_block_35_z), .Z(nonrestoring_block_27_z), .Cin(nonrestoring_block_37_cout), .Sel(Q_2),
    .Cout(nonrestoring_block_27_cout), .B(B5));
  nonrestoring_block nonrestoring_block_28 (
    .A(nonrestoring_block_37_z), .Z(nonrestoring_block_28_z), .Cin(nonrestoring_block_39_cout), .Sel(Q_3),
    .Cout(nonrestoring_block_28_cout), .B(B5));
  nonrestoring_block nonrestoring_block_29 (
    .A(nonrestoring_block_39_z), .Z(nonrestoring_block_29_z), .Cin(nonrestoring_block_41_cout), .Sel(Q_4),
    .Cout(nonrestoring_block_29_cout), .B(B5));
  nonrestoring_block nonrestoring_block_30 (
    .A(nonrestoring_block_41_z), .Z(nonrestoring_block_30_z), .Cin(nonrestoring_block_44_cout), .Sel(Q_5),
    .Cout(nonrestoring_block_30_cout), .B(B5));
  nonrestoring_block nonrestoring_block_31 (
    .A(nonrestoring_block_44_z), .Z(nonrestoring_block_31_z), .Cin(nonrestoring_block_46_cout), .Sel(Q_6),
    .Cout(nonrestoring_block_31_cout), .B(B5));
  nonrestoring_block nonrestoring_block_32 (
    .A(nonrestoring_block_46_z), .Z(nonrestoring_block_32_z), .Cin(nonrestoring_block_48_cout), .Sel(Q_7),
    .Cout(nonrestoring_block_32_cout), .B(B5));
  restoring_block restoring_block_3 (
    .A(nonrestoring_block_32_z), .B(B5), .Z(R5), .Cin(restoring_block_5_cout), .Cout(restoring_block_3_cout),
    .Sel(nonrestoring_block_16_z));
  nonrestoring_block nonrestoring_block_33 (
    .A(1'b0), .Z(nonrestoring_block_33_z), .Cin(nonrestoring_block_34_cout), .Sel(1'b1),
    .Cout(nonrestoring_block_33_cout), .B(B4));
  nonrestoring_block nonrestoring_block_34 (
    .A(1'b0), .Z(nonrestoring_block_34_z), .Cin(nonrestoring_block_49_cout), .Sel(1'b1),
    .Cout(nonrestoring_block_34_cout), .B(B3));
  nonrestoring_block nonrestoring_block_35 (
    .A(nonrestoring_block_34_z), .Z(nonrestoring_block_35_z), .Cin(nonrestoring_block_36_cout), .Sel(Q),
    .Cout(nonrestoring_block_35_cout), .B(B4));
  nonrestoring_block nonrestoring_block_36 (
    .A(nonrestoring_block_49_z), .Z(nonrestoring_block_36_z), .Cin(nonrestoring_block_50_cout), .Sel(Q),
    .Cout(nonrestoring_block_36_cout), .B(B3));
  nonrestoring_block nonrestoring_block_37 (
    .A(nonrestoring_block_36_z), .Z(nonrestoring_block_37_z), .Cin(nonrestoring_block_38_cout), .Sel(Q_2),
    .Cout(nonrestoring_block_37_cout), .B(B4));
  nonrestoring_block nonrestoring_block_38 (
    .A(nonrestoring_block_50_z), .Z(nonrestoring_block_38_z), .Cin(nonrestoring_block_51_cout), .Sel(Q_2),
    .Cout(nonrestoring_block_38_cout), .B(B3));
  nonrestoring_block nonrestoring_block_39 (
    .A(nonrestoring_block_38_z), .Z(nonrestoring_block_39_z), .Cin(nonrestoring_block_40_cout), .Sel(Q_3),
    .Cout(nonrestoring_block_39_cout), .B(B4));
  nonrestoring_block nonrestoring_block_40 (
    .A(nonrestoring_block_51_z), .Z(nonrestoring_block_40_z), .Cin(nonrestoring_block_52_cout), .Sel(Q_3),
    .Cout(nonrestoring_block_40_cout), .B(B3));
  nonrestoring_block nonrestoring_block_41 (
    .A(nonrestoring_block_40_z), .Z(nonrestoring_block_41_z), .Cin(nonrestoring_block_42_cout), .Sel(Q_4),
    .Cout(nonrestoring_block_41_cout), .B(B4));
  nonrestoring_block nonrestoring_block_42 (
    .A(nonrestoring_block_52_z), .Z(nonrestoring_block_42_z), .Cin(nonrestoring_block_53_cout), .Sel(Q_4),
    .Cout(nonrestoring_block_42_cout), .B(B3));
  nonrestoring_block nonrestoring_block_43 (
    .A(nonrestoring_block_53_z), .Z(nonrestoring_block_43_z), .Cin(nonrestoring_block_54_cout), .Sel(Q_5),
    .Cout(nonrestoring_block_43_cout), .B(B3));
  nonrestoring_block nonrestoring_block_44 (
    .A(nonrestoring_block_42_z), .Z(nonrestoring_block_44_z), .Cin(nonrestoring_block_43_cout), .Sel(Q_5),
    .Cout(nonrestoring_block_44_cout), .B(B4));
  nonrestoring_block nonrestoring_block_45 (
    .A(nonrestoring_block_54_z), .Z(nonrestoring_block_45_z), .Cin(nonrestoring_block_55_cout), .Sel(Q_6),
    .Cout(nonrestoring_block_45_cout), .B(B3));
  nonrestoring_block nonrestoring_block_46 (
    .A(nonrestoring_block_43_z), .Z(nonrestoring_block_46_z), .Cin(nonrestoring_block_45_cout), .Sel(Q_6),
    .Cout(nonrestoring_block_46_cout), .B(B4));
  nonrestoring_block nonrestoring_block_47 (
    .A(nonrestoring_block_55_z), .Z(nonrestoring_block_47_z), .Cin(nonrestoring_block_56_cout), .Sel(Q_7),
    .Cout(nonrestoring_block_47_cout), .B(B3));
  nonrestoring_block nonrestoring_block_48 (
    .A(nonrestoring_block_45_z), .Z(nonrestoring_block_48_z), .Cin(nonrestoring_block_47_cout), .Sel(Q_7),
    .Cout(nonrestoring_block_48_cout), .B(B4));
  restoring_block restoring_block_4 (
    .A(nonrestoring_block_47_z), .B(B3), .Z(R3), .Cin(restoring_block_6_cout), .Cout(restoring_block_4_cout),
    .Sel(nonrestoring_block_16_z));
  restoring_block restoring_block_5 (
    .A(nonrestoring_block_48_z), .B(B4), .Z(R4), .Cin(restoring_block_4_cout), .Cout(restoring_block_5_cout),
    .Sel(nonrestoring_block_16_z));
  nonrestoring_block nonrestoring_block_49 (
    .A(1'b0), .Z(nonrestoring_block_49_z), .Cin(nonrestoring_block_57_cout), .Sel(1'b1),
    .Cout(nonrestoring_block_49_cout), .B(B2));
  nonrestoring_block nonrestoring_block_50 (
    .A(nonrestoring_block_57_z), .Z(nonrestoring_block_50_z), .Cin(nonrestoring_block_58_cout), .Sel(Q),
    .Cout(nonrestoring_block_50_cout), .B(B2));
  nonrestoring_block nonrestoring_block_51 (
    .A(nonrestoring_block_58_z), .Z(nonrestoring_block_51_z), .Cin(nonrestoring_block_59_cout), .Sel(Q_2),
    .Cout(nonrestoring_block_51_cout), .B(B2));
  nonrestoring_block nonrestoring_block_52 (
    .A(nonrestoring_block_59_z), .Z(nonrestoring_block_52_z), .Cin(nonrestoring_block_60_cout), .Sel(Q_3),
    .Cout(nonrestoring_block_52_cout), .B(B2));
  nonrestoring_block nonrestoring_block_53 (
    .A(nonrestoring_block_60_z), .Z(nonrestoring_block_53_z), .Cin(nonrestoring_block_61_cout), .Sel(Q_4),
    .Cout(nonrestoring_block_53_cout), .B(B2));
  nonrestoring_block nonrestoring_block_54 (
    .A(nonrestoring_block_61_z), .Z(nonrestoring_block_54_z), .Cin(nonrestoring_block_62_cout), .Sel(Q_5),
    .Cout(nonrestoring_block_54_cout), .B(B2));
  nonrestoring_block nonrestoring_block_55 (
    .A(nonrestoring_block_62_z), .Z(nonrestoring_block_55_z), .Cin(nonrestoring_block_63_cout), .Sel(Q_6),
    .Cout(nonrestoring_block_55_cout), .B(B2));
  nonrestoring_block nonrestoring_block_56 (
    .A(nonrestoring_block_63_z), .Z(nonrestoring_block_56_z), .Cin(nonrestoring_block_64_cout), .Sel(Q_7),
    .Cout(nonrestoring_block_56_cout), .B(B2));
  restoring_block restoring_block_6 (
    .A(nonrestoring_block_56_z), .B(B2), .Z(R2), .Cin(restoring_block_7_cout), .Cout(restoring_block_6_cout),
    .Sel(nonrestoring_block_16_z));
  nonrestoring_block nonrestoring_block_57 (
    .A(1'b0), .Z(nonrestoring_block_57_z), .Cin(nonrestoring_block_65_cout), .Sel(1'b1),
    .Cout(nonrestoring_block_57_cout), .B(B1));
  nonrestoring_block nonrestoring_block_58 (
    .A(nonrestoring_block_65_z), .Z(nonrestoring_block_58_z), .Cin(nonrestoring_block_66_cout), .Sel(Q),
    .Cout(nonrestoring_block_58_cout), .B(B1));
  nonrestoring_block nonrestoring_block_59 (
    .A(nonrestoring_block_66_z), .Z(nonrestoring_block_59_z), .Cin(nonrestoring_block_67_cout), .Sel(Q_2),
    .Cout(nonrestoring_block_59_cout), .B(B1));
  nonrestoring_block nonrestoring_block_60 (
    .A(nonrestoring_block_67_z), .Z(nonrestoring_block_60_z), .Cin(nonrestoring_block_68_cout), .Sel(Q_3),
    .Cout(nonrestoring_block_60_cout), .B(B1));
  nonrestoring_block nonrestoring_block_61 (
    .A(nonrestoring_block_68_z), .Z(nonrestoring_block_61_z), .Cin(nonrestoring_block_69_cout), .Sel(Q_4),
    .Cout(nonrestoring_block_61_cout), .B(B1));
  nonrestoring_block nonrestoring_block_62 (
    .A(nonrestoring_block_69_z), .Z(nonrestoring_block_62_z), .Cin(nonrestoring_block_70_cout), .Sel(Q_5),
    .Cout(nonrestoring_block_62_cout), .B(B1));
  nonrestoring_block nonrestoring_block_63 (
    .A(nonrestoring_block_70_z), .Z(nonrestoring_block_63_z), .Cin(nonrestoring_block_71_cout), .Sel(Q_6),
    .Cout(nonrestoring_block_63_cout), .B(B1));
  nonrestoring_block nonrestoring_block_64 (
    .A(nonrestoring_block_71_z), .Z(nonrestoring_block_64_z), .Cin(nonrestoring_block_72_cout), .Sel(Q_7),
    .Cout(nonrestoring_block_64_cout), .B(B1));
  restoring_block restoring_block_7 (
    .A(nonrestoring_block_64_z), .B(B1), .Z(R1), .Cin(restoring_block_8_cout), .Cout(restoring_block_7_cout),
    .Sel(nonrestoring_block_16_z));
  nonrestoring_block nonrestoring_block_65 (
    .A(A7), .Z(nonrestoring_block_65_z), .Cin(1'b1), .Sel(1'b1), .Cout(nonrestoring_block_65_cout), .B(B0));
  nonrestoring_block nonrestoring_block_66 (
    .A(A6), .Z(nonrestoring_block_66_z), .Cin(Q), .Sel(Q), .Cout(nonrestoring_block_66_cout), .B(B0));
  nonrestoring_block nonrestoring_block_67 (
    .A(A6_2), .Z(nonrestoring_block_67_z), .Cin(Q_2), .Sel(Q_2), .Cout(nonrestoring_block_67_cout), .B(B0));
  nonrestoring_block nonrestoring_block_68 (
    .A(A6_3), .Z(nonrestoring_block_68_z), .Cin(Q_3), .Sel(Q_3), .Cout(nonrestoring_block_68_cout), .B(B0));
  nonrestoring_block nonrestoring_block_69 (
    .A(A6_4), .Z(nonrestoring_block_69_z), .Cin(Q_4), .Sel(Q_4), .Cout(nonrestoring_block_69_cout), .B(B0));
  nonrestoring_block nonrestoring_block_70 (
    .A(A6_5), .Z(nonrestoring_block_70_z), .Cin(Q_5), .Sel(Q_5), .Cout(nonrestoring_block_70_cout), .B(B0));
  nonrestoring_block nonrestoring_block_71 (
    .A(A6_6), .Z(nonrestoring_block_71_z), .Cin(Q_6), .Sel(Q_6), .Cout(nonrestoring_block_71_cout), .B(B0));
  nonrestoring_block nonrestoring_block_72 (
    .A(A6_7), .Z(nonrestoring_block_72_z), .Cin(Q_7), .Sel(Q_7), .Cout(nonrestoring_block_72_cout), .B(B0));
  restoring_block restoring_block_8 (
    .A(nonrestoring_block_72_z), .B(B0), .Z(R0), .Cin(1'b0), .Cout(restoring_block_8_cout),
    .Sel(nonrestoring_block_16_z));
endmodule

// ns
module nonrestoring_block (
  input  Cin,
  input  A,
  input  B,
  input  Sel,
  output Z,
  output Cout
);

  wire xor_1_out;

  Adder #(.width(1)) adder_1 (.a(A), .b(xor_1_out), .out(Z), .cin(Cin), .cout(Cout));
  xor xor_1 (xor_1_out, B, Sel);
endmodule

module restoringv2 (
  input  B7,
  input  B6,
  input  B5,
  input  B4,
  input  B3,
  input  B2,
  input  B1,
  input  B0,
  input  A7,
  input  A6,
  input  A5,
  input  A4,
  input  A3,
  input  A2,
  input  A1,
  input  A0,
  output Q7,
  output Q6,
  output Q5,
  output Q4,
  output Q3,
  output Q2,
  output Q1,
  output Q0,
  output R7,
  output R6,
  output R5,
  output R4,
  output R3,
  output R2,
  output R1,
  output R0
);

  wire not_1_out, not_3_out, not_5_out, not_7_out, restoringv2_block_2_cout, restoringv2_block_2_z,
       restoringv2_block_3_cout, restoringv2_block_3_z, restoringv2_block_5_cout, restoringv2_block_5_z,
       restoringv2_block_8_cout, restoringv2_block_8_z, restoringv2_block_10_cout, restoringv2_block_10_z,
       restoringv2_block_11_cout, restoringv2_block_11_z, restoringv2_block_14_cout, restoringv2_block_14_z,
       restoringv2_block_16_cout, restoringv2_block_16_z, restoringv2_block_17_cout, restoringv2_block_17_z,
       restoringv2_block_18_cout, restoringv2_block_18_z, restoringv2_block_19_cout, restoringv2_block_19_z,
       restoringv2_block_20_cout, restoringv2_block_20_z, restoringv2_block_21_cout, restoringv2_block_21_z,
       restoringv2_block_22_cout, restoringv2_block_22_z, restoringv2_block_23_cout, restoringv2_block_23_z,
       restoringv2_block_24_cout, restoringv2_block_25_cout, restoringv2_block_25_z,
       restoringv2_block_26_cout, restoringv2_block_26_z, restoringv2_block_27_cout, restoringv2_block_27_z,
       restoringv2_block_28_cout, restoringv2_block_28_z, restoringv2_block_29_cout, restoringv2_block_29_z,
       restoringv2_block_30_cout, restoringv2_block_30_z, restoringv2_block_31_cout, restoringv2_block_31_z,
       restoringv2_block_32_cout, restoringv2_block_32_z, restoringv2_block_33_cout, restoringv2_block_33_z,
       restoringv2_block_34_cout, restoringv2_block_34_z, restoringv2_block_35_cout, restoringv2_block_35_z,
       restoringv2_block_36_cout, restoringv2_block_36_z, restoringv2_block_37_cout, restoringv2_block_37_z,
       restoringv2_block_38_cout, restoringv2_block_38_z, restoringv2_block_39_cout, restoringv2_block_39_z,
       restoringv2_block_40_cout, restoringv2_block_40_z, restoringv2_block_41_cout, restoringv2_block_41_z,
       restoringv2_block_42_cout, restoringv2_block_42_z, restoringv2_block_43_cout, restoringv2_block_43_z,
       restoringv2_block_44_cout, restoringv2_block_44_z, restoringv2_block_45_cout, restoringv2_block_45_z,
       restoringv2_block_46_cout, restoringv2_block_46_z, restoringv2_block_47_cout, restoringv2_block_47_z,
       restoringv2_block_48_cout, restoringv2_block_49_cout, restoringv2_block_49_z,
       restoringv2_block_50_cout, restoringv2_block_50_z, restoringv2_block_51_cout, restoringv2_block_51_z,
       restoringv2_block_52_cout, restoringv2_block_52_z, restoringv2_block_53_cout, restoringv2_block_53_z,
       restoringv2_block_54_cout, restoringv2_block_54_z, restoringv2_block_55_cout, restoringv2_block_55_z,
       restoringv2_block_56_cout, restoringv2_block_57_cout, restoringv2_block_57_z,
       restoringv2_block_58_cout, restoringv2_block_58_z, restoringv2_block_59_cout, restoringv2_block_59_z,
       restoringv2_block_60_cout, restoringv2_block_60_z, restoringv2_block_61_cout, restoringv2_block_61_z,
       restoringv2_block_62_cout, restoringv2_block_62_z, restoringv2_block_63_cout, restoringv2_block_63_z,
       restoringv2_block_64_cout, restoringv2_block_64_z;

  not not_1 (not_1_out, B6);
  restoringv2_block restoringv2_block_1 (
    .A(1'b1), .B(B7), .Cin(restoringv2_block_2_cout), .Cout(Q7), .Sel(Q7));  // open: Z
  restoringv2_block restoringv2_block_2 (
    .A(1'b0), .B(not_1_out), .Z(restoringv2_block_2_z), .Cin(restoringv2_block_17_cout),
    .Cout(restoringv2_block_2_cout), .Sel(Q7));
  restoringv2_block restoringv2_block_3 (
    .A(restoringv2_block_17_z), .B(not_1_out), .Z(restoringv2_block_3_z), .Cin(restoringv2_block_18_cout),
    .Cout(restoringv2_block_3_cout), .Sel(Q6));
  restoringv2_block restoringv2_block_4 (
    .A(restoringv2_block_2_z), .B(B7), .Cin(restoringv2_block_3_cout), .Cout(Q6), .Sel(Q6));  // open: Z
  restoringv2_block restoringv2_block_5 (
    .A(restoringv2_block_18_z), .B(not_1_out), .Z(restoringv2_block_5_z), .Cin(restoringv2_block_19_cout),
    .Cout(restoringv2_block_5_cout), .Sel(Q5));
  restoringv2_block restoringv2_block_6 (
    .A(restoringv2_block_3_z), .B(B7), .Cin(restoringv2_block_5_cout), .Cout(Q5), .Sel(Q5));  // open: Z
  restoringv2_block restoringv2_block_7 (
    .A(restoringv2_block_5_z), .B(B7), .Cin(restoringv2_block_8_cout), .Cout(Q4), .Sel(Q4));  // open: Z
  restoringv2_block restoringv2_block_8 (
    .A(restoringv2_block_19_z), .B(not_1_out), .Z(restoringv2_block_8_z), .Cin(restoringv2_block_20_cout),
    .Cout(restoringv2_block_8_cout), .Sel(Q4));
  restoringv2_block restoringv2_block_9 (
    .A(restoringv2_block_8_z), .B(B7), .Cin(restoringv2_block_10_cout), .Cout(Q3), .Sel(Q3));  // open: Z
  restoringv2_block restoringv2_block_10 (
    .A(restoringv2_block_20_z), .B(not_1_out), .Z(restoringv2_block_10_z), .Cin(restoringv2_block_21_cout),
    .Cout(restoringv2_block_10_cout), .Sel(Q3));
  restoringv2_block restoringv2_block_11 (
    .A(restoringv2_block_21_z), .B(not_1_out), .Z(restoringv2_block_11_z), .Cin(restoringv2_block_22_cout),
    .Cout(restoringv2_block_11_cout), .Sel(Q2));
  restoringv2_block restoringv2_block_12 (
    .A(restoringv2_block_10_z), .B(B7), .Cin(restoringv2_block_11_cout), .Cout(Q2), .Sel(Q2));  // open: Z
  restoringv2_block restoringv2_block_13 (
    .A(restoringv2_block_11_z), .B(B7), .Cin(restoringv2_block_14_cout), .Cout(Q1), .Sel(Q1));  // open: Z
  restoringv2_block restoringv2_block_14 (
    .A(restoringv2_block_22_z), .B(not_1_out), .Z(restoringv2_block_14_z), .Cin(restoringv2_block_23_cout),
    .Cout(restoringv2_block_14_cout), .Sel(Q1));
  restoringv2_block restoringv2_block_15 (
    .A(restoringv2_block_14_z), .B(B7), .Z(R7), .Cin(restoringv2_block_16_cout), .Cout(Q0), .Sel(Q0));
  restoringv2_block restoringv2_block_16 (
    .A(restoringv2_block_23_z), .B(not_1_out), .Z(restoringv2_block_16_z), .Cin(restoringv2_block_24_cout),
    .Cout(restoringv2_block_16_cout), .Sel(Q0));
  restoringv2_block restoringv2_block_17 (
    .A(1'b1), .B(B5), .Z(restoringv2_block_17_z), .Cin(restoringv2_block_25_cout),
    .Cout(restoringv2_block_17_cout), .Sel(Q7));
  restoringv2_block restoringv2_block_18 (
    .A(restoringv2_block_25_z), .B(B5), .Z(restoringv2_block_18_z), .Cin(restoringv2_block_26_cout),
    .Cout(restoringv2_block_18_cout), .Sel(Q6));
  restoringv2_block restoringv2_block_19 (
    .A(restoringv2_block_26_z), .B(B5), .Z(restoringv2_block_19_z), .Cin(restoringv2_block_27_cout),
    .Cout(restoringv2_block_19_cout), .Sel(Q5));
  restoringv2_block restoringv2_block_20 (
    .A(restoringv2_block_27_z), .B(B5), .Z(restoringv2_block_20_z), .Cin(restoringv2_block_28_cout),
    .Cout(restoringv2_block_20_cout), .Sel(Q4));
  restoringv2_block restoringv2_block_21 (
    .A(restoringv2_block_28_z), .B(B5), .Z(restoringv2_block_21_z), .Cin(restoringv2_block_29_cout),
    .Cout(restoringv2_block_21_cout), .Sel(Q3));
  restoringv2_block restoringv2_block_22 (
    .A(restoringv2_block_29_z), .B(B5), .Z(restoringv2_block_22_z), .Cin(restoringv2_block_30_cout),
    .Cout(restoringv2_block_22_cout), .Sel(Q2));
  restoringv2_block restoringv2_block_23 (
    .A(restoringv2_block_30_z), .B(B5), .Z(restoringv2_block_23_z), .Cin(restoringv2_block_31_cout),
    .Cout(restoringv2_block_23_cout), .Sel(Q1));
  restoringv2_block restoringv2_block_24 (
    .A(restoringv2_block_31_z), .B(B5), .Z(R5), .Cin(restoringv2_block_32_cout),
    .Cout(restoringv2_block_24_cout), .Sel(Q0));
  not not_2 (R6, restoringv2_block_16_z);
  not not_3 (not_3_out, B4);
  restoringv2_block restoringv2_block_25 (
    .A(1'b0), .B(not_3_out), .Z(restoringv2_block_25_z), .Cin(restoringv2_block_33_cout),
    .Cout(restoringv2_block_25_cout), .Sel(Q7));
  restoringv2_block restoringv2_block_26 (
    .A(restoringv2_block_33_z), .B(not_3_out), .Z(restoringv2_block_26_z), .Cin(restoringv2_block_35_cout),
    .Cout(restoringv2_block_26_cout), .Sel(Q6));
  restoringv2_block restoringv2_block_27 (
    .A(restoringv2_block_35_z), .B(not_3_out), .Z(restoringv2_block_27_z), .Cin(restoringv2_block_38_cout),
    .Cout(restoringv2_block_27_cout), .Sel(Q5));
  restoringv2_block restoringv2_block_28 (
    .A(restoringv2_block_38_z), .B(not_3_out), .Z(restoringv2_block_28_z), .Cin(restoringv2_block_39_cout),
    .Cout(restoringv2_block_28_cout), .Sel(Q4));
  restoringv2_block restoringv2_block_29 (
    .A(restoringv2_block_39_z), .B(not_3_out), .Z(restoringv2_block_29_z), .Cin(restoringv2_block_42_cout),
    .Cout(restoringv2_block_29_cout), .Sel(Q3));
  restoringv2_block restoringv2_block_30 (
    .A(restoringv2_block_42_z), .B(not_3_out), .Z(restoringv2_block_30_z), .Cin(restoringv2_block_43_cout),
    .Cout(restoringv2_block_30_cout), .Sel(Q2));
  restoringv2_block restoringv2_block_31 (
    .A(restoringv2_block_43_z), .B(not_3_out), .Z(restoringv2_block_31_z), .Cin(restoringv2_block_46_cout),
    .Cout(restoringv2_block_31_cout), .Sel(Q1));
  restoringv2_block restoringv2_block_32 (
    .A(restoringv2_block_46_z), .B(not_3_out), .Z(restoringv2_block_32_z), .Cin(restoringv2_block_48_cout),
    .Cout(restoringv2_block_32_cout), .Sel(Q0));
  not not_4 (R4, restoringv2_block_32_z);
  not not_5 (not_5_out, B2);
  restoringv2_block restoringv2_block_33 (
    .A(1'b1), .B(B3), .Z(restoringv2_block_33_z), .Cin(restoringv2_block_34_cout),
    .Cout(restoringv2_block_33_cout), .Sel(Q7));
  restoringv2_block restoringv2_block_34 (
    .A(1'b0), .B(not_5_out), .Z(restoringv2_block_34_z), .Cin(restoringv2_block_49_cout),
    .Cout(restoringv2_block_34_cout), .Sel(Q7));
  restoringv2_block restoringv2_block_35 (
    .A(restoringv2_block_34_z), .B(B3), .Z(restoringv2_block_35_z), .Cin(restoringv2_block_36_cout),
    .Cout(restoringv2_block_35_cout), .Sel(Q6));
  restoringv2_block restoringv2_block_36 (
    .A(restoringv2_block_49_z), .B(not_5_out), .Z(restoringv2_block_36_z), .Cin(restoringv2_block_50_cout),
    .Cout(restoringv2_block_36_cout), .Sel(Q6));
  restoringv2_block restoringv2_block_37 (
    .A(restoringv2_block_50_z), .B(not_5_out), .Z(restoringv2_block_37_z), .Cin(restoringv2_block_51_cout),
    .Cout(restoringv2_block_37_cout), .Sel(Q5));
  restoringv2_block restoringv2_block_38 (
    .A(restoringv2_block_36_z), .B(B3), .Z(restoringv2_block_38_z), .Cin(restoringv2_block_37_cout),
    .Cout(restoringv2_block_38_cout), .Sel(Q5));
  restoringv2_block restoringv2_block_39 (
    .A(restoringv2_block_37_z), .B(B3), .Z(restoringv2_block_39_z), .Cin(restoringv2_block_40_cout),
    .Cout(restoringv2_block_39_cout), .Sel(Q4));
  restoringv2_block restoringv2_block_40 (
    .A(restoringv2_block_51_z), .B(not_5_out), .Z(restoringv2_block_40_z), .Cin(restoringv2_block_52_cout),
    .Cout(restoringv2_block_40_cout), .Sel(Q4));
  restoringv2_block restoringv2_block_41 (
    .A(restoringv2_block_52_z), .B(not_5_out), .Z(restoringv2_block_41_z), .Cin(restoringv2_block_53_cout),
    .Cout(restoringv2_block_41_cout), .Sel(Q3));
  restoringv2_block restoringv2_block_42 (
    .A(restoringv2_block_40_z), .B(B3), .Z(restoringv2_block_42_z), .Cin(restoringv2_block_41_cout),
    .Cout(restoringv2_block_42_cout), .Sel(Q3));
  restoringv2_block restoringv2_block_43 (
    .A(restoringv2_block_41_z), .B(B3), .Z(restoringv2_block_43_z), .Cin(restoringv2_block_44_cout),
    .Cout(restoringv2_block_43_cout), .Sel(Q2));
  restoringv2_block restoringv2_block_44 (
    .A(restoringv2_block_53_z), .B(not_5_out), .Z(restoringv2_block_44_z), .Cin(restoringv2_block_54_cout),
    .Cout(restoringv2_block_44_cout), .Sel(Q2));
  restoringv2_block restoringv2_block_45 (
    .A(restoringv2_block_54_z), .B(not_5_out), .Z(restoringv2_block_45_z), .Cin(restoringv2_block_55_cout),
    .Cout(restoringv2_block_45_cout), .Sel(Q1));
  restoringv2_block restoringv2_block_46 (
    .A(restoringv2_block_44_z), .B(B3), .Z(restoringv2_block_46_z), .Cin(restoringv2_block_45_cout),
    .Cout(restoringv2_block_46_cout), .Sel(Q1));
  restoringv2_block restoringv2_block_47 (
    .A(restoringv2_block_55_z), .B(not_5_out), .Z(restoringv2_block_47_z), .Cin(restoringv2_block_56_cout),
    .Cout(restoringv2_block_47_cout), .Sel(Q0));
  restoringv2_block restoringv2_block_48 (
    .A(restoringv2_block_45_z), .B(B3), .Z(R3), .Cin(restoringv2_block_47_cout),
    .Cout(restoringv2_block_48_cout), .Sel(Q0));
  restoringv2_block restoringv2_block_49 (
    .A(1'b1), .B(B1), .Z(restoringv2_block_49_z), .Cin(restoringv2_block_57_cout),
    .Cout(restoringv2_block_49_cout), .Sel(Q7));
  restoringv2_block restoringv2_block_50 (
    .A(restoringv2_block_57_z), .B(B1), .Z(restoringv2_block_50_z), .Cin(restoringv2_block_58_cout),
    .Cout(restoringv2_block_50_cout), .Sel(Q6));
  restoringv2_block restoringv2_block_51 (
    .A(restoringv2_block_58_z), .B(B1), .Z(restoringv2_block_51_z), .Cin(restoringv2_block_59_cout),
    .Cout(restoringv2_block_51_cout), .Sel(Q5));
  restoringv2_block restoringv2_block_52 (
    .A(restoringv2_block_59_z), .B(B1), .Z(restoringv2_block_52_z), .Cin(restoringv2_block_60_cout),
    .Cout(restoringv2_block_52_cout), .Sel(Q4));
  restoringv2_block restoringv2_block_53 (
    .A(restoringv2_block_60_z), .B(B1), .Z(restoringv2_block_53_z), .Cin(restoringv2_block_61_cout),
    .Cout(restoringv2_block_53_cout), .Sel(Q3));
  restoringv2_block restoringv2_block_54 (
    .A(restoringv2_block_61_z), .B(B1), .Z(restoringv2_block_54_z), .Cin(restoringv2_block_62_cout),
    .Cout(restoringv2_block_54_cout), .Sel(Q2));
  restoringv2_block restoringv2_block_55 (
    .A(restoringv2_block_62_z), .B(B1), .Z(restoringv2_block_55_z), .Cin(restoringv2_block_63_cout),
    .Cout(restoringv2_block_55_cout), .Sel(Q1));
  restoringv2_block restoringv2_block_56 (
    .A(restoringv2_block_63_z), .B(B1), .Z(R1), .Cin(restoringv2_block_64_cout),
    .Cout(restoringv2_block_56_cout), .Sel(Q0));
  not not_6 (R2, restoringv2_block_47_z);
  not not_7 (not_7_out, B0);
  restoringv2_block restoringv2_block_57 (
    .A(A7), .B(not_7_out), .Z(restoringv2_block_57_z), .Cin(1'b1), .Cout(restoringv2_block_57_cout), .Sel(Q7));
  restoringv2_block restoringv2_block_58 (
    .A(A6), .B(not_7_out), .Z(restoringv2_block_58_z), .Cin(1'b1), .Cout(restoringv2_block_58_cout), .Sel(Q6));
  restoringv2_block restoringv2_block_59 (
    .A(A5), .B(not_7_out), .Z(restoringv2_block_59_z), .Cin(1'b1), .Cout(restoringv2_block_59_cout), .Sel(Q5));
  restoringv2_block restoringv2_block_60 (
    .A(A4), .B(not_7_out), .Z(restoringv2_block_60_z), .Cin(1'b1), .Cout(restoringv2_block_60_cout), .Sel(Q4));
  restoringv2_block restoringv2_block_61 (
    .A(A3), .B(not_7_out), .Z(restoringv2_block_61_z), .Cin(1'b1), .Cout(restoringv2_block_61_cout), .Sel(Q3));
  restoringv2_block restoringv2_block_62 (
    .A(A2), .B(not_7_out), .Z(restoringv2_block_62_z), .Cin(1'b1), .Cout(restoringv2_block_62_cout), .Sel(Q2));
  restoringv2_block restoringv2_block_63 (
    .A(A1), .B(not_7_out), .Z(restoringv2_block_63_z), .Cin(1'b1), .Cout(restoringv2_block_63_cout), .Sel(Q1));
  restoringv2_block restoringv2_block_64 (
    .A(A0), .B(not_7_out), .Z(restoringv2_block_64_z), .Cin(1'b1), .Cout(restoringv2_block_64_cout), .Sel(Q0));
  not not_8 (R0, restoringv2_block_64_z);
endmodule

// rs_2
module restoringv2_block (
  input  B,
  input  A,
  input  Cin,
  input  Sel,
  output Cout,
  output Z
);

  wire mirror_adder_1_s, not_1_out;

  mirror_adder mirror_adder_1 (.A(A), .B(B), .S(mirror_adder_1_s), .Cin(Cin), .Cout(Cout));
  not not_1 (not_1_out, A);
  single_mux single_mux_1 (.Sel(Sel), .S1(mirror_adder_1_s), .S0(not_1_out), .S(Z));
endmodule

// ma
module mirror_adder (
  input  Cin,
  input  A,
  input  B,
  output S,
  output Cout
);

  wire adder_1_cout, adder_1_out;

  not not_1 (Cout, adder_1_cout);
  not not_2 (S, adder_1_out);
  Adder #(.width(1)) adder_1 (.a(A), .b(B), .out(adder_1_out), .cin(Cin), .cout(adder_1_cout));
endmodule

// row_3
module restoring3_row (
  input  B7,
  input  A7,
  input  B6,
  input  A6,
  input  B5,
  input  A5,
  input  B4,
  input  A4,
  input  B3,
  input  A3,
  input  B2,
  input  A2,
  input  B1,
  input  A1,
  input  B0,
  input  A0,
  output Cout,
  output Z7,
  output Z6,
  output Z5,
  output Z4,
  output Z3,
  output Z2,
  output Z1,
  output Z0
);

  wire double_mux_1_c, double_mux_1_s, double_mux_2_c, double_mux_2_s, double_mux_3_c, double_mux_3_s,
       double_mux_4_c, double_mux_4_s, double_mux_5_s, double_mux_6_c, double_mux_6_s, double_mux_7_c,
       double_mux_7_s, double_mux_8_c, double_mux_8_s, double_mux_9_c, double_mux_9_s, double_mux_10_c,
       double_mux_10_s, double_mux_11_c, double_mux_11_s, mirror_adder_1_cout, mirror_adder_1_s,
       mirror_adder_2_cout, mirror_adder_2_s, mirror_adder_3_cout, mirror_adder_3_s, mirror_adder_4_cout,
       mirror_adder_4_s, mirror_adder_5_cout, mirror_adder_5_s, mirror_adder_6_cout, mirror_adder_6_s,
       mirror_adder_7_cout, mirror_adder_7_s, mirror_adder_8_cout, mirror_adder_8_s, mirror_adder_9_cout,
       mirror_adder_9_s, mirror_adder_10_cout, mirror_adder_10_s, mirror_adder_11_cout, mirror_adder_11_s,
       mirror_adder_12_cout, mirror_adder_12_s, mirror_adder_13_cout, mirror_adder_13_s,
       mirror_adder_14_cout, mirror_adder_14_s, mirror_adder_15_cout, mirror_adder_15_s, not_1_out,
       not_2_out, not_3_out, not_4_out, not_5_out, not_6_out, not_7_out, not_8_out, single_mux_2_s,
       single_mux_3_s, single_mux_4_s, single_mux_6_s, single_mux_8_s, single_mux_11_s;

  mirror_adder mirror_adder_1 (.A(A7), .B(B7), .S(mirror_adder_1_s), .Cin(1'b0), .Cout(mirror_adder_1_cout));
  mirror_adder mirror_adder_2 (.A(A7), .B(B7), .S(mirror_adder_2_s), .Cin(1'b1), .Cout(mirror_adder_2_cout));
  double_mux double_mux_1 (
    .Sel(mirror_adder_3_cout), .C0(mirror_adder_1_cout), .C1(mirror_adder_2_cout), .S0(mirror_adder_1_s),
    .S1(mirror_adder_2_s), .C(double_mux_1_c), .S(double_mux_1_s));
  double_mux double_mux_2 (
    .Sel(mirror_adder_4_cout), .C0(mirror_adder_1_cout), .C1(mirror_adder_2_cout), .S0(mirror_adder_1_s),
    .S1(mirror_adder_2_s), .C(double_mux_2_c), .S(double_mux_2_s));
  double_mux double_mux_3 (
    .Sel(double_mux_6_c), .C0(double_mux_1_c), .C1(double_mux_2_c), .S0(double_mux_1_s), .S1(double_mux_2_s),
    .C(double_mux_3_c), .S(double_mux_3_s));
  double_mux double_mux_4 (
    .Sel(double_mux_7_c), .C0(double_mux_1_c), .C1(double_mux_2_c), .S0(double_mux_1_s), .S1(double_mux_2_s),
    .C(double_mux_4_c), .S(double_mux_4_s));
  double_mux double_mux_5 (
    .Sel(double_mux_10_c), .C0(double_mux_3_c), .C1(double_mux_4_c), .S0(double_mux_3_s),
    .S1(double_mux_4_s), .C(Cout), .S(double_mux_5_s));
  single_mux single_mux_1 (.Sel(Cout), .S1(double_mux_5_s), .S0(not_1_out), .S(Z7));
  not not_1 (not_1_out, A7);
  mirror_adder mirror_adder_3 (.A(A6), .B(B6), .S(mirror_adder_3_s), .Cin(1'b0), .Cout(mirror_adder_3_cout));
  mirror_adder mirror_adder_4 (.A(A6), .B(B6), .S(mirror_adder_4_s), .Cin(1'b1), .Cout(mirror_adder_4_cout));
  single_mux single_mux_2 (.Sel(double_mux_6_c), .S1(mirror_adder_4_s), .S0(mirror_adder_3_s), .S(single_mux_2_s));
  single_mux single_mux_3 (.Sel(double_mux_7_c), .S1(mirror_adder_4_s), .S0(mirror_adder_3_s), .S(single_mux_3_s));
  single_mux single_mux_4 (.Sel(double_mux_10_c), .S1(single_mux_3_s), .S0(single_mux_2_s), .S(single_mux_4_s));
  single_mux single_mux_5 (.Sel(Cout), .S1(single_mux_4_s), .S0(not_2_out), .S(Z6));
  not not_2 (not_2_out, A6);
  mirror_adder mirror_adder_5 (.A(A5), .B(B5), .S(mirror_adder_5_s), .Cin(1'b0), .Cout(mirror_adder_5_cout));
  mirror_adder mirror_adder_6 (.A(A5), .B(B5), .S(mirror_adder_6_s), .Cin(1'b1), .Cout(mirror_adder_6_cout));
  double_mux double_mux_6 (
    .Sel(mirror_adder_7_cout), .C0(mirror_adder_5_cout), .C1(mirror_adder_6_cout), .S0(mirror_adder_5_s),
    .S1(mirror_adder_6_s), .C(double_mux_6_c), .S(double_mux_6_s));
  double_mux double_mux_7 (
    .Sel(mirror_adder_8_cout), .C0(mirror_adder_5_cout), .C1(mirror_adder_6_cout), .S0(mirror_adder_5_s),
    .S1(mirror_adder_6_s), .C(double_mux_7_c), .S(double_mux_7_s));
  single_mux single_mux_6 (.Sel(double_mux_10_c), .S1(double_mux_7_s), .S0(double_mux_6_s), .S(single_mux_6_s));
  single_mux single_mux_7 (.Sel(Cout), .S1(single_mux_6_s), .S0(not_3_out), .S(Z5));
  not not_3 (not_3_out, A5);
  mirror_adder mirror_adder_7 (.A(A4), .B(B4), .S(mirror_adder_7_s), .Cin(1'b0), .Cout(mirror_adder_7_cout));
  mirror_adder mirror_adder_8 (.A(A4), .B(B4), .S(mirror_adder_8_s), .Cin(1'b1), .Cout(mirror_adder_8_cout));
  single_mux single_mux_8 (.Sel(double_mux_10_c), .S1(mirror_adder_8_s), .S0(mirror_adder_7_s), .S(single_mux_8_s));
  single_mux single_mux_9 (.Sel(Cout), .S1(single_mux_8_s), .S0(not_4_out), .S(Z4));
  not not_4 (not_4_out, A4);
  mirror_adder mirror_adder_9 (.A(A3), .B(B3), .S(mirror_adder_9_s), .Cin(1'b0), .Cout(mirror_adder_9_cout));
  mirror_adder mirror_adder_10 (.A(A3), .B(B3), .S(mirror_adder_10_s), .Cin(1'b1), .Cout(mirror_adder_10_cout));
  double_mux double_mux_8 (
    .Sel(mirror_adder_11_cout), .C0(mirror_adder_9_cout), .C1(mirror_adder_10_cout), .S0(mirror_adder_9_s),
    .S1(mirror_adder_10_s), .C(double_mux_8_c), .S(double_mux_8_s));
  double_mux double_mux_9 (
    .Sel(mirror_adder_12_cout), .C0(mirror_adder_9_cout), .C1(mirror_adder_10_cout), .S0(mirror_adder_9_s),
    .S1(mirror_adder_10_s), .C(double_mux_9_c), .S(double_mux_9_s));
  double_mux double_mux_10 (
    .Sel(double_mux_11_c), .C0(double_mux_8_c), .C1(double_mux_9_c), .S0(double_mux_8_s),
    .S1(double_mux_9_s), .C(double_mux_10_c), .S(double_mux_10_s));
  single_mux single_mux_10 (.Sel(Cout), .S1(double_mux_10_s), .S0(not_5_out), .S(Z3));
  not not_5 (not_5_out, A3);
  mirror_adder mirror_adder_11 (.A(A2), .B(B2), .S(mirror_adder_11_s), .Cin(1'b0), .Cout(mirror_adder_11_cout));
  mirror_adder mirror_adder_12 (.A(A2), .B(B2), .S(mirror_adder_12_s), .Cin(1'b1), .Cout(mirror_adder_12_cout));
  single_mux single_mux_11 (.Sel(double_mux_11_c), .S1(mirror_adder_12_s), .S0(mirror_adder_11_s), .S(single_mux_11_s));
  single_mux single_mux_12 (.Sel(Cout), .S1(single_mux_11_s), .S0(not_6_out), .S(Z2));
  not not_6 (not_6_out, A2);
  mirror_adder mirror_adder_13 (.A(A1), .B(B1), .S(mirror_adder_13_s), .Cin(1'b0), .Cout(mirror_adder_13_cout));
  mirror_adder mirror_adder_14 (.A(A1), .B(B1), .S(mirror_adder_14_s), .Cin(1'b1), .Cout(mirror_adder_14_cout));
  double_mux double_mux_11 (
    .Sel(mirror_adder_15_cout), .C0(mirror_adder_13_cout), .C1(mirror_adder_14_cout), .S0(mirror_adder_13_s),
    .S1(mirror_adder_14_s), .C(double_mux_11_c), .S(double_mux_11_s));
  single_mux single_mux_13 (.Sel(Cout), .S1(double_mux_11_s), .S0(not_7_out), .S(Z1));
  not not_7 (not_7_out, A1);
  mirror_adder mirror_adder_15 (.A(A0), .B(B0), .S(mirror_adder_15_s), .Cin(1'b1), .Cout(mirror_adder_15_cout));
  single_mux single_mux_14 (.Sel(Cout), .S1(mirror_adder_15_s), .S0(not_8_out), .S(Z0));
  not not_8 (not_8_out, A0);
endmodule

// cs
module double_mux (
  input  C1,
  input  S1,
  input  C0,
  input  S0,
  input  Sel,
  output C,
  output S
);

  Multiplexer #(.enable("false")) multiplexer_1 (.in0(S0), .in1(S1), .out(S), .sel(Sel));
  Multiplexer #(.enable("false")) multiplexer_2 (.in0(C0), .in1(C1), .out(C), .sel(Sel));
endmodule

// s
module single_mux (
  input  S1,
  input  S0,
  input  Sel,
  output S
);

  Multiplexer #(.enable("false")) multiplexer_1 (.in0(S0), .in1(S1), .out(S), .sel(Sel));
endmodule

module restoringv3 (
  input  B7,
  input  B6,
  input  B5,
  input  B4,
  input  B3,
  input  B2,
  input  B1,
  input  B0,
  input  A7,
  input  A6,
  input  A5,
  input  A4,
  input  A3,
  input  A2,
  input  A1,
  input  A0,
  output Q7,
  output Q6,
  output Q5,
  output Q4,
  output Q3,
  output Q2,
  output Q1,
  output Q0,
  output R7,
  output R6,
  output R5,
  output R4,
  output R3,
  output R2,
  output R1,
  output R0
);

  wire not_1_out, not_3_out, not_5_out, not_7_out, restoring3_row_1_z0, restoring3_row_1_z1,
       restoring3_row_1_z2, restoring3_row_1_z3, restoring3_row_1_z4, restoring3_row_1_z5,
       restoring3_row_1_z6, restoring3_row_2_z0, restoring3_row_2_z1, restoring3_row_2_z2,
       restoring3_row_2_z3, restoring3_row_2_z4, restoring3_row_2_z5, restoring3_row_2_z6,
       restoring3_row_3_z0, restoring3_row_3_z1, restoring3_row_3_z2, restoring3_row_3_z3,
       restoring3_row_3_z4, restoring3_row_3_z5, restoring3_row_3_z6, restoring3_row_4_z0,
       restoring3_row_4_z1, restoring3_row_4_z2, restoring3_row_4_z3, restoring3_row_4_z4,
       restoring3_row_4_z5, restoring3_row_4_z6, restoring3_row_5_z0, restoring3_row_5_z1,
       restoring3_row_5_z2, restoring3_row_5_z3, restoring3_row_5_z4, restoring3_row_5_z5,
       restoring3_row_5_z6, restoring3_row_6_z0, restoring3_row_6_z1, restoring3_row_6_z2,
       restoring3_row_6_z3, restoring3_row_6_z4, restoring3_row_6_z5, restoring3_row_6_z6,
       restoring3_row_7_z0, restoring3_row_7_z1, restoring3_row_7_z2, restoring3_row_7_z3,
       restoring3_row_7_z4, restoring3_row_7_z5, restoring3_row_7_z6, restoring3_row_8_z0,
       restoring3_row_8_z2, restoring3_row_8_z4, restoring3_row_8_z6;

  restoring3_row restoring3_row_1 (
    .Cout(Q7), .B7(B7), .A7(1'b1), .B6(not_1_out), .A6(1'b0), .B5(B5), .A5(1'b1), .B4(not_3_out), .A4(1'b0),
    .B3(B3), .A3(1'b1), .B2(not_5_out), .A2(1'b0), .B1(B1), .A1(1'b1), .B0(not_7_out), .A0(A7),
    .Z6(restoring3_row_1_z6), .Z5(restoring3_row_1_z5), .Z4(restoring3_row_1_z4), .Z3(restoring3_row_1_z3),
    .Z2(restoring3_row_1_z2), .Z1(restoring3_row_1_z1), .Z0(restoring3_row_1_z0));  // open: Z7
  restoring3_row restoring3_row_2 (
    .Cout(Q6), .B7(B7), .A7(restoring3_row_1_z6), .B6(not_1_out), .A6(restoring3_row_1_z5), .B5(B5),
    .A5(restoring3_row_1_z4), .B4(not_3_out), .A4(restoring3_row_1_z3), .B3(B3), .A3(restoring3_row_1_z2),
    .B2(not_5_out), .A2(restoring3_row_1_z1), .B1(B1), .A1(restoring3_row_1_z0), .B0(not_7_out), .A0(A6),
    .Z6(restoring3_row_2_z6), .Z5(restoring3_row_2_z5), .Z4(restoring3_row_2_z4), .Z3(restoring3_row_2_z3),
    .Z2(restoring3_row_2_z2), .Z1(restoring3_row_2_z1), .Z0(restoring3_row_2_z0));  // open: Z7
  restoring3_row restoring3_row_3 (
    .Cout(Q5), .B7(B7), .A7(restoring3_row_2_z6), .B6(not_1_out), .A6(restoring3_row_2_z5), .B5(B5),
    .A5(restoring3_row_2_z4), .B4(not_3_out), .A4(restoring3_row_2_z3), .B3(B3), .A3(restoring3_row_2_z2),
    .B2(not_5_out), .A2(restoring3_row_2_z1), .B1(B1), .A1(restoring3_row_2_z0), .B0(not_7_out), .A0(A5),
    .Z6(restoring3_row_3_z6), .Z5(restoring3_row_3_z5), .Z4(restoring3_row_3_z4), .Z3(restoring3_row_3_z3),
    .Z2(restoring3_row_3_z2), .Z1(restoring3_row_3_z1), .Z0(restoring3_row_3_z0));  // open: Z7
  restoring3_row restoring3_row_4 (
    .Cout(Q4), .B7(B7), .A7(restoring3_row_3_z6), .B6(not_1_out), .A6(restoring3_row_3_z5), .B5(B5),
    .A5(restoring3_row_3_z4), .B4(not_3_out), .A4(restoring3_row_3_z3), .B3(B3), .A3(restoring3_row_3_z2),
    .B2(not_5_out), .A2(restoring3_row_3_z1), .B1(B1), .A1(restoring3_row_3_z0), .B0(not_7_out), .A0(A4),
    .Z6(restoring3_row_4_z6), .Z5(restoring3_row_4_z5), .Z4(restoring3_row_4_z4), .Z3(restoring3_row_4_z3),
    .Z2(restoring3_row_4_z2), .Z1(restoring3_row_4_z1), .Z0(restoring3_row_4_z0));  // open: Z7
  restoring3_row restoring3_row_5 (
    .Cout(Q3), .B7(B7), .A7(restoring3_row_4_z6), .B6(not_1_out), .A6(restoring3_row_4_z5), .B5(B5),
    .A5(restoring3_row_4_z4), .B4(not_3_out), .A4(restoring3_row_4_z3), .B3(B3), .A3(restoring3_row_4_z2),
    .B2(not_5_out), .A2(restoring3_row_4_z1), .B1(B1), .A1(restoring3_row_4_z0), .B0(not_7_out), .A0(A3),
    .Z6(restoring3_row_5_z6), .Z5(restoring3_row_5_z5), .Z4(restoring3_row_5_z4), .Z3(restoring3_row_5_z3),
    .Z2(restoring3_row_5_z2), .Z1(restoring3_row_5_z1), .Z0(restoring3_row_5_z0));  // open: Z7
  restoring3_row restoring3_row_6 (
    .Cout(Q2), .B7(B7), .A7(restoring3_row_5_z6), .B6(not_1_out), .A6(restoring3_row_5_z5), .B5(B5),
    .A5(restoring3_row_5_z4), .B4(not_3_out), .A4(restoring3_row_5_z3), .B3(B3), .A3(restoring3_row_5_z2),
    .B2(not_5_out), .A2(restoring3_row_5_z1), .B1(B1), .A1(restoring3_row_5_z0), .B0(not_7_out), .A0(A2),
    .Z6(restoring3_row_6_z6), .Z5(restoring3_row_6_z5), .Z4(restoring3_row_6_z4), .Z3(restoring3_row_6_z3),
    .Z2(restoring3_row_6_z2), .Z1(restoring3_row_6_z1), .Z0(restoring3_row_6_z0));  // open: Z7
  restoring3_row restoring3_row_7 (
    .Cout(Q1), .B7(B7), .A7(restoring3_row_6_z6), .B6(not_1_out), .A6(restoring3_row_6_z5), .B5(B5),
    .A5(restoring3_row_6_z4), .B4(not_3_out), .A4(restoring3_row_6_z3), .B3(B3), .A3(restoring3_row_6_z2),
    .B2(not_5_out), .A2(restoring3_row_6_z1), .B1(B1), .A1(restoring3_row_6_z0), .B0(not_7_out), .A0(A1),
    .Z6(restoring3_row_7_z6), .Z5(restoring3_row_7_z5), .Z4(restoring3_row_7_z4), .Z3(restoring3_row_7_z3),
    .Z2(restoring3_row_7_z2), .Z1(restoring3_row_7_z1), .Z0(restoring3_row_7_z0));  // open: Z7
  restoring3_row restoring3_row_8 (
    .Cout(Q0), .B7(B7), .A7(restoring3_row_7_z6), .B6(not_1_out), .A6(restoring3_row_7_z5), .B5(B5),
    .A5(restoring3_row_7_z4), .B4(not_3_out), .A4(restoring3_row_7_z3), .B3(B3), .A3(restoring3_row_7_z2),
    .B2(not_5_out), .A2(restoring3_row_7_z1), .B1(B1), .A1(restoring3_row_7_z0), .B0(not_7_out), .A0(A0),
    .Z7(R7), .Z6(restoring3_row_8_z6), .Z5(R5), .Z4(restoring3_row_8_z4), .Z3(R3), .Z2(restoring3_row_8_z2),
    .Z1(R1), .Z0(restoring3_row_8_z0));
  not not_1 (not_1_out, B6);
  not not_2 (R6, restoring3_row_8_z6);
  not not_3 (not_3_out, B4);
  not not_4 (R4, restoring3_row_8_z4);
  not not_5 (not_5_out, B2);
  not not_6 (R2, restoring3_row_8_z2);
  not not_7 (not_7_out, B0);
  not not_8 (R0, restoring3_row_8_z0);
endmodule
